// Logisim project Banco de regs.circ as structural Verilog: 2 circuits, main circuit Registrador
module Registrador (
  input  in_1,
  input  [7:0] VALOR,
  output [7:0] \SAÍDA 
);

  D_Flip_Flop d_ff_1 (.clk(in_1), .D(VALOR[7]), .Q(\SAÍDA [7]));  // open: Qn, preset, en, reset
  D_Flip_Flop d_ff_2 (.clk(in_1), .D(VALOR[6]), .Q(\SAÍDA [6]));  // open: Qn, preset, en, reset
  D_Flip_Flop d_ff_3 (.clk(in_1), .D(VALOR[5]), .Q(\SAÍDA [5]));  // open: Qn, preset, en, reset
  D_Flip_Flop d_ff_4 (.clk(in_1), .D(VALOR[4]), .Q(\SAÍDA [4]));  // open: Qn, preset, en, reset
  D_Flip_Flop d_ff_5 (.clk(in_1), .D(VALOR[3]), .Q(\SAÍDA [3]));  // open: Qn, preset, en, reset
  D_Flip_Flop d_ff_6 (.clk(in_1), .D(VALOR[2]), .Q(\SAÍDA [2]));  // open: Qn, preset, en, reset
  D_Flip_Flop d_ff_7 (.clk(in_1), .D(VALOR[1]), .Q(\SAÍDA [1]));  // open: Qn, preset, en, reset
  D_Flip_Flop d_ff_8 (.clk(in_1), .D(VALOR[0]), .Q(\SAÍDA [0]));  // open: Qn, preset, en, reset
endmodule

module BCR (
  input  in_1,
  input  in_2,
  input  [7:0] in_3,
  input  [1:0] in_4,
  input  [1:0] in_5,
  output [7:0] out_6,
  output [7:0] out_7
);

  wire demultiplexer_1_out0, demultiplexer_1_out1, demultiplexer_1_out2, demultiplexer_1_out3;
  wire [7:0] register_1_q, register_2_q, register_3_q, register_4_q;

  Demultiplexer #(.select(2)) demultiplexer_1 (
    .out0(demultiplexer_1_out0), .out1(demultiplexer_1_out1), .out2(demultiplexer_1_out2),
    .out3(demultiplexer_1_out3), .in(in_2), .sel(in_4));  // open: en
  Register register_1 (.D(in_3), .en(demultiplexer_1_out0), .Q(register_1_q), .clk(in_1));  // open: clr
  Register register_2 (.D(in_3), .en(demultiplexer_1_out1), .Q(register_2_q), .clk(in_1));  // open: clr
  Register register_3 (.D(in_3), .en(demultiplexer_1_out2), .Q(register_3_q), .clk(in_1));  // open: clr
  Register register_4 (.D(in_3), .en(demultiplexer_1_out3), .Q(register_4_q), .clk(in_1));  // open: clr
  Multiplexer #(.select(2), .width(8)) multiplexer_1 (
    .in0(register_1_q), .in1(register_2_q), .in2(register_3_q), .in3(register_4_q), .out(out_6), .sel(in_4));  // open: en
  Multiplexer #(.select(2), .width(8)) multiplexer_2 (
    .in0(register_1_q), .in1(register_2_q), .in2(register_3_q), .in3(register_4_q), .out(out_7), .sel(in_5));  // open: en
endmodule
