// Logisim project PROCESSADOR FINAL.circ as structural Verilog: 1 circuit, main circuit main
module main (
  input  [7:0] in_1,
  input  [7:0] A,
  input  [7:0] B,
  input  in_4,
  input  in_5,
  input  in_6,
  input  [3:0] op,
  input  in_8,
  input  in_9,
  output [7:0] out_10,
  output [7:0] \SAÍDA ,
  output [2:0] out_12
);

  wire and_1_out, and_2_out, clock_1_out, clock_2_out, clock_3_out, not_1_out, not_2_out, not_3_out,
       not_4_out, unidade_de_controle_1_alusrc, unidade_de_controle_1_branch,
       \unidade_de_controle_1_endereço , unidade_de_controle_1_jump, unidade_de_controle_1_mem_write,
       unidade_de_controle_1_regwrite;
  wire [1:0] unidade_de_controle_1_memomreg;
  wire [7:0] bcr_1_out_7, multiplexer_1_out, multiplexer_3_out, ram_2_data;
  wire [11:8] ram_1_data;

  not not_1 (not_1_out, and_1_out);
  Counter counter_1 (
    .load(not_1_out), .D(in_1), .count(and_1_out), .Q(out_10), .clk(clock_1_out), .clr(in_4));  // open: carry
  and and_1 (and_1_out, not_2_out, not_3_out);
  Clock clock_1 (.out(clock_1_out));
  buf and_2 (and_2_out, unidade_de_controle_1_branch);  // AND_Gate
  not not_2 (not_2_out, and_2_out);
  not not_3 (not_3_out, unidade_de_controle_1_jump);
  RAM #(.dataWidth(16)) ram_1 (
    .addr(out_10), .data({op, ram_1_data, in_1}), .clk(clock_1_out), .ld(in_6), .clr(in_5));  // open: sel
  Unidade_de_controle unidade_de_controle_1 (
    .\ENDEREÇO (\unidade_de_controle_1_endereço ), .JUMP(unidade_de_controle_1_jump),
    .BRANCH(unidade_de_controle_1_branch), .MEMOMREG(unidade_de_controle_1_memomreg), .ALUOP(out_12),
    .MEM_WRITE(unidade_de_controle_1_mem_write), .ALUSRC(unidade_de_controle_1_alusrc),
    .REGWRITE(unidade_de_controle_1_regwrite), .in_1(op));
  Multiplexer #(.select(2), .width(8)) multiplexer_1 (
    .in0(in_1), .in1(ram_2_data), .in3(\SAÍDA ), .out(multiplexer_1_out), .sel(unidade_de_controle_1_memomreg));  // open: in2, en
  Clock clock_2 (.out(clock_2_out));
  BCR bcr_1 (
    .in_1(clock_2_out), .in_2(unidade_de_controle_1_regwrite), .in_3(multiplexer_1_out),
    .in_4(ram_1_data[9:8]), .in_5(ram_1_data[11:10]), .out_6(A), .out_7(bcr_1_out_7));
  ULA ula_1 (.A(B), .B(A), .in_3(out_12), .\SAÍDA (\SAÍDA ));
  Multiplexer #(.width(8)) multiplexer_2 (
    .in0(bcr_1_out_7), .in1(in_1), .out(B), .sel(unidade_de_controle_1_alusrc));  // open: en
  Multiplexer #(.width(8)) multiplexer_3 (
    .in0(\SAÍDA ), .in1(in_1), .out(multiplexer_3_out), .sel(\unidade_de_controle_1_endereço ));  // open: en
  RAM ram_2 (
    .addr(multiplexer_3_out), .data(ram_2_data), .sel(unidade_de_controle_1_mem_write), .clk(clock_3_out),
    .ld(in_8), .clr(in_9));
  Clock clock_3 (.out(clock_3_out));
  assign ram_2_data = not_4_out ? bcr_1_out_7 : 8'bz;  // Controlled_Buffer controlled_buffer_1
  not not_4 (not_4_out, in_8);

  // Notes on the sheet:
  //   Memória RAM
  //   SINAIS OP
  //   0100 - OR
  //   0000 - NOT
  //   0001 - AND
  //   0010 - NOR
  //   0011- XOR
  //   0101 - SOMA
  //   0110 - SUBTRAÇÃO
  //   0111 - NOT
endmodule
