// Logisim project Unidade de controle.circ as structural Verilog: 1 circuit, main circuit Unidade de controle
module Unidade_de_controle (
  input  [3:0] in_1,
  output \ENDEREÇO ,
  output JUMP,
  output BRANCH,
  output [1:0] MEMOMREG,
  output [2:0] ALUOP,
  output MEM_WRITE,
  output ALUSRC,
  output REGWRITE
);

  Multiplexer #(.select(4), .width(11)) multiplexer_1 (
    .in0(11'h4e8), .in1(11'h4c8), .in2(11'h4a8), .in3(11'h488), .in4(11'h468), .in5(11'h448), .in6(11'h411),
    .in7(11'h101), .in8(11'h2), .in9(11'h24), .in10(11'h628), .in11(11'h428), .in12(11'h608), .in13(11'h408),
    .out({REGWRITE, ALUSRC, MEM_WRITE, ALUOP, MEMOMREG, BRANCH, JUMP, \ENDEREÇO }), .sel(in_1));  // open: in14, in15, en

  // Notes on the sheet:
  //   sinais de controle
  //   1101 ADD
  //   0101 AND
  //   0110 LOAD
  //   0111 STORE
  //   1000 JUMP
  //   1001 BEQ
  //   1010 SUBI
  //   1011 SUB
  //   1100 ADDI
  //   0000 NOT
  //   0001 XOR
  //   0010 NOR
  //   0011 OR
  //   0100 NAND
endmodule
